# Fritzing sketch phototransistor (saved by Fritzing 0.9.3b)
breadboards: 1

parts:
  Raspberry_Pi_1 = Raspberry Pi 3 [part_number=RPI-3-V1.2]
  IC1 = MCP3008 8-channel 10-bit ADC [part_number=MCP3008]
  Q2 = LTR-301 [package=ltr-301]
  R1 = Resistor [tolerance=±5% resistance=1k package=THT]

nets:
  N1: Raspberry_Pi_1.GIPO10, IC1.no_name_yet#11
  N2: Raspberry_Pi_1.GIPO9, IC1.no_name_yet#12
  N3: Raspberry_Pi_1.GIPO11, IC1.no_name_yet#13
  N4: Raspberry_Pi_1.GIPO8, IC1.no_name_yet#10
  N5: Raspberry_Pi_1.GND, IC1.no_name_yet#9, IC1.no_name_yet#14, R1.Pin_0
  N6: Raspberry_Pi_1.5V, IC1.no_name_yet#15, IC1.no_name_yet#16, Q2.C
  N7: IC1.no_name_yet#1, Q2.E, R1.Pin_1
